# Fritzing sketch esquema fritzing despertadorSolar (saved by Fritzing 1.0.4)
breadboards: 1

parts:
  LCD2004-I2C1 = LCD2004-I2C
  Componente1 = Arduino Nano (Rev3.0)
  S1 = Momentary Switch [package=ksa_sealed_tac_switch]
  S2 = Momentary Switch [package=ksa_sealed_tac_switch]
  S3 = Momentary Switch [package=ksa_sealed_tac_switch]
  S4 = Momentary Switch [package=ksa_sealed_tac_switch]
  LED1 = LED - 5mm [color="Infrared (940nm)" current=0.030A package="5 mm [THT]"]
  LED2 = LED - 5mm [color="Infrared (940nm)" current=0.030A package="5 mm [THT]"]
  LED3 = LED - 5mm [color="Infrared (940nm)" current=30mA package="5 mm [THT]"]
  R1 = Resistor [tolerance=±5% resistance=330 package="2010 [SMD]"]
  R2 = Resistor [tolerance=±5% resistance=330 package="2010 [SMD]"]
  R3 = Resistor [tolerance=±5% resistance=330 package="2010 [SMD]"]
  R4 = Resistor [tolerance=±5% resistance=10k package="2010 [SMD]"]
  R5 = Resistor [tolerance=±5% resistance=10k package="2010 [SMD]"]
  R6 = Resistor [tolerance=±5% resistance=10k package="2010 [SMD]"]
  R7 = Resistor [tolerance=±5% resistance=10k package="2010 [SMD]"]
  A1 = MH-FMD buzzer
  ZS-042_RTC1 = ZS-042 RTC Module

nets:
  GND: LCD2004-I2C1.GND, Componente1.GND, S1.4, S2.4, S3.4, S4.4, R4.Pin_1, R5.Pin_1, R6.Pin_1, R7.Pin_1
  VCC: LCD2004-I2C1.VCC, Componente1.VIN
  N1: LCD2004-I2C1.SDA, Componente1.A5, ZS-042_RTC1.SCL
  N2: LCD2004-I2C1.SCL, Componente1.A4, ZS-042_RTC1.SDA
  N3: Componente1.D2, S1.1
  N4: Componente1.D3, S2.1
  N5: Componente1.D4, S3.1
  N6: Componente1.D5, S4.1
  N7: Componente1.D7, R1.Pin_0
  N8: Componente1.D8, R2.Pin_0
  N9: Componente1.D9, R3.Pin_0
  N10: Componente1.D10, A1.Pin_2
  N11: S1.2, R4.Pin_0
  N12: S2.2, R5.Pin_0
  N13: S3.2, R6.Pin_0
  N14: S4.2, R7.Pin_0
  N15: LED1.cathode, LED2.cathode, LED3.cathode, A1.Pin_3, ZS-042_RTC1.GND
  N16: LED1.anode, R1.Pin_1
  N17: LED2.anode, R2.Pin_1
  N18: LED3.anode, R3.Pin_1
  N19: A1.Pin_1, ZS-042_RTC1.VCC

custom parts:
  LCD2004-I2C: A standard character display with 4x20 characters. Comes in many colors with LCM2004 IIC attached.
  MH-FMD buzzer: MH-FMD buzzer.
